// Logisim project 6551071040_LAB2_Bai2Trang5.circ as structural Verilog: 1 circuit, main circuit main
module main (
  input  A,
  input  B,
  input  C,
  output Y
);

  wire xor_1_out;

  xor xor_1 (xor_1_out, A, B);
  and and_1 (Y, xor_1_out, C);

  // Notes on the sheet:
  //   Phạm Tuấn Hưng - MSSV:6551071040
endmodule
